// Digital circuit 4to16Decoder.dig as structural Verilog
module _4to16Decoder (
  input  [3:0] Input,
  input  Enable,
  output Output0,
  output Output1,
  output Output2,
  output Output3,
  output Output4,
  output Output5,
  output Output6,
  output Output7,
  output Output8,
  output Output9,
  output Output10,
  output Output11,
  output Output12,
  output Output13,
  output Output14,
  output Output15
);

  and and_1 (Output0, ~Input[0], ~Input[1], ~Input[2], ~Input[3], Enable);  // And
  and and_2 (Output1, Input[0], ~Input[1], ~Input[2], ~Input[3], Enable);  // And
  and and_3 (Output2, ~Input[0], Input[1], ~Input[2], ~Input[3], Enable);  // And
  and and_4 (Output3, Input[0], Input[1], ~Input[2], ~Input[3], Enable);  // And
  and and_5 (Output4, ~Input[0], ~Input[1], Input[2], ~Input[3], Enable);  // And
  and and_6 (Output5, Input[0], ~Input[1], Input[2], ~Input[3], Enable);  // And
  and and_7 (Output6, ~Input[0], Input[1], Input[2], ~Input[3], Enable);  // And
  and and_8 (Output7, Input[0], Input[1], Input[2], ~Input[3], Enable);  // And
  and and_9 (Output8, ~Input[0], ~Input[1], ~Input[2], Input[3], Enable);  // And
  and and_10 (Output9, Input[0], ~Input[1], ~Input[2], Input[3], Enable);  // And
  and and_11 (Output10, ~Input[0], Input[1], ~Input[2], Input[3], Enable);  // And
  and and_12 (Output11, Input[0], Input[1], ~Input[2], Input[3], Enable);  // And
  and and_13 (Output12, ~Input[0], ~Input[1], Input[2], Input[3], Enable);  // And
  and and_14 (Output13, Input[0], ~Input[1], Input[2], Input[3], Enable);  // And
  and and_15 (Output14, ~Input[0], Input[1], Input[2], Input[3], Enable);  // And
  and and_16 (Output15, Input[0], Input[1], Input[2], Input[3], Enable);
endmodule
