// Digital circuit RegisterFile.dig as structural Verilog
module RegisterFile (
  input  [3:0] ReadReg0,
  input  [3:0] ReadReg1,
  input  [3:0] WriteReg,
  input  [31:0] WriteData,
  input  WriteEN,
  input  CLK,
  input  [31:0] PC,
  output [31:0] RD0,
  output [31:0] RD1,
  output [31:0] r0,
  output [31:0] r1,
  output [31:0] r2,
  output [31:0] r3,
  output [31:0] r4,
  output [31:0] r5,
  output [31:0] r6,
  output [31:0] r7,
  output [31:0] r8,
  output [31:0] r9,
  output [31:0] r10,
  output [31:0] r11,
  output [31:0] r12,
  output [31:0] r13,
  output [31:0] r14,
  output [31:0] r15
);

  wire _4to16decoder_1_output0, _4to16decoder_1_output1, _4to16decoder_1_output2, _4to16decoder_1_output3,
       _4to16decoder_1_output4, _4to16decoder_1_output5, _4to16decoder_1_output6, _4to16decoder_1_output7,
       _4to16decoder_1_output8, _4to16decoder_1_output9, _4to16decoder_1_output10, _4to16decoder_1_output11,
       _4to16decoder_1_output12, _4to16decoder_1_output13, _4to16decoder_1_output14;

  // Probe on r0
  Register #(.Bits(32)) u_r0 (.D(WriteData), .C(CLK), .en(_4to16decoder_1_output0), .Q(r0));
  // Probe on r1
  Register #(.Bits(32)) u_r1 (.D(WriteData), .C(CLK), .en(_4to16decoder_1_output1), .Q(r1));
  // Probe on r2
  Register #(.Bits(32)) u_r2 (.D(WriteData), .C(CLK), .en(_4to16decoder_1_output2), .Q(r2));
  Multiplexer #(.Selector_Bits(4), .Bits(32)) multiplexer_1 (
    .sel(ReadReg0), .in_0(r0), .in_1(r1), .in_2(r2), .in_3(r3), .in_4(r4), .in_5(r5), .in_6(r6), .in_7(r7),
    .in_8(r8), .in_9(r9), .in_10(r10), .in_11(r11), .in_12(r12), .in_13(r13), .in_14(r14), .in_15(PC),
    .out(RD0));
  // Probe on r3
  Register #(.Bits(32)) u_r3 (.D(WriteData), .C(CLK), .en(_4to16decoder_1_output3), .Q(r3));
  // Probe on r4
  Register #(.Bits(32)) u_r4 (.D(WriteData), .C(CLK), .en(_4to16decoder_1_output4), .Q(r4));
  // Probe on r5
  Register #(.Bits(32)) u_r5 (.D(WriteData), .C(CLK), .en(_4to16decoder_1_output5), .Q(r5));
  // Probe on r6
  Register #(.Bits(32)) u_r6 (.D(WriteData), .C(CLK), .en(_4to16decoder_1_output6), .Q(r6));
  _4to16Decoder _4to16decoder_1 (
    .Input(WriteReg), .Enable(WriteEN), .Output0(_4to16decoder_1_output0), .Output1(_4to16decoder_1_output1),
    .Output2(_4to16decoder_1_output2), .Output3(_4to16decoder_1_output3), .Output4(_4to16decoder_1_output4),
    .Output5(_4to16decoder_1_output5), .Output6(_4to16decoder_1_output6), .Output7(_4to16decoder_1_output7),
    .Output8(_4to16decoder_1_output8), .Output9(_4to16decoder_1_output9),
    .Output10(_4to16decoder_1_output10), .Output11(_4to16decoder_1_output11),
    .Output12(_4to16decoder_1_output12), .Output13(_4to16decoder_1_output13),
    .Output14(_4to16decoder_1_output14));  // open: Output15
  // Probe on r7
  Register #(.Bits(32)) u_r7 (.D(WriteData), .C(CLK), .en(_4to16decoder_1_output7), .Q(r7));
  // Probe on r8
  Register #(.Bits(32)) u_r8 (.D(WriteData), .C(CLK), .en(_4to16decoder_1_output8), .Q(r8));
  // Probe on r9
  Register #(.Bits(32)) u_r9 (.D(WriteData), .C(CLK), .en(_4to16decoder_1_output9), .Q(r9));
  Multiplexer #(.Selector_Bits(4), .Bits(32)) multiplexer_2 (
    .sel(ReadReg1), .in_0(r0), .in_1(r1), .in_2(r2), .in_3(r3), .in_4(r4), .in_5(r5), .in_6(r6), .in_7(r7),
    .in_8(r8), .in_9(r9), .in_10(r10), .in_11(r11), .in_12(r12), .in_13(r13), .in_14(r14), .in_15(PC),
    .out(RD1));
  // Probe on r10
  Register #(.Bits(32)) u_r10 (.D(WriteData), .C(CLK), .en(_4to16decoder_1_output10), .Q(r10));
  // Probe on r11
  Register #(.Bits(32)) u_r11 (.D(WriteData), .C(CLK), .en(_4to16decoder_1_output11), .Q(r11));
  // Probe on r12
  Register #(.Bits(32)) u_r12 (.D(WriteData), .C(CLK), .en(_4to16decoder_1_output12), .Q(r12));
  // Probe on r13
  Register #(.Bits(32)) u_r13 (.D(WriteData), .C(CLK), .en(_4to16decoder_1_output13), .Q(r13));
  // Probe on r14
  Register #(.Bits(32)) u_r14 (.D(WriteData), .C(CLK), .en(_4to16decoder_1_output14), .Q(r14));

  assign r15 = PC;

  // Other names for the same wires on the sheet: Q0[31:0] = r0; Q1[31:0] = r1; Q2[31:0] = r2; Q3[31:0] = r3;
  //   Q4[31:0] = r4; Q5[31:0] = r5; Q6[31:0] = r6; Q7[31:0] = r7; Q8[31:0] = r8; Q9[31:0] = r9; Q10[31:0] = r10;
  //   Q11[31:0] = r11; Q12[31:0] = r12; Q13[31:0] = r13; Q14[31:0] = r14; Q15[31:0] = PC
endmodule
