// Digital circuit conditional_control_unit.dig as structural Verilog
module conditional_control_unit (
  input  [31:0] iw,
  input  [3:0] NZCV,
  input  CLK,
  output RFW,
  output [1:0] EXT,
  output [1:0] ALUop,
  output ALU1src,
  output BR,
  output BL,
  output BX,
  output mul,
  output MR,
  output MW
);

  wire AL_eq, and_1_out, and_2_out, and_3_out, and_4_out, C, comparator_1_eq, comparator_2_eq, EQ_eq, GT_eq,
       LT_eq, main_decoder_br, main_decoder_cmp, N, NE_eq, or_1_out, V, Z;

  control_unit main_decoder (
    .iw(iw), .RFW(RFW), .EXT(EXT), .ALUop(ALUop), .ALU1src(ALU1src), .BR(main_decoder_br), .BL(BL), .BX(BX),
    .mul(mul), .MR(MR), .MW(MW), .cmp(main_decoder_cmp));
  Register #(.Bits(4)) register_1 (.D(NZCV), .C(CLK), .en(main_decoder_cmp), .Q({V, C, Z, N}));
  Comparator #(.Bits(4)) AL (.a(iw[31:28]), .b(4'b1110), .eq(AL_eq));  // open: gt, lt
  Comparator #(.Bits(4)) EQ (.a(iw[31:28]), .b(4'b0000), .eq(EQ_eq));  // open: gt, lt
  Comparator #(.Bits(4)) NE (.a(iw[31:28]), .b(4'b0001), .eq(NE_eq));  // open: gt, lt
  Comparator #(.Bits(4)) LT (.a(iw[31:28]), .b(4'b1011), .eq(LT_eq));  // open: gt, lt
  Comparator comparator_1 (.a(N), .b(V), .eq(comparator_1_eq));  // open: gt, lt
  Comparator #(.Bits(4)) GT (.a(iw[31:28]), .b(4'b1100), .eq(GT_eq));  // open: gt, lt
  Comparator comparator_2 (.a(N), .b(V), .eq(comparator_2_eq));  // open: gt, lt
  and and_1 (and_1_out, Z, EQ_eq);
  and and_2 (and_2_out, ~Z, NE_eq);  // And
  and and_3 (and_3_out, LT_eq, ~comparator_1_eq);  // And
  and and_4 (and_4_out, GT_eq, ~Z, comparator_2_eq);  // And
  or or_1 (or_1_out, AL_eq, and_1_out, and_2_out, and_3_out, and_4_out);
  and and_5 (BR, main_decoder_br, or_1_out);
endmodule
