// Digital circuit instruction_memory.dig as structural Verilog
module instruction_memory (
  input  [31:0] A,
  input  [3:0] PN,
  output [31:0] D
);

  wire [31:0] _0_quadratic_d, _1_sum_array_5_d, _2_find_max_5_d, _3_fib_iter_10_d, _4_fib_iter_19_d,
       _5_fib_rec_10_d, _6_fib_rec_19_d;

  ROM #(.AddrBits(5), .Bits(32)) _0_quadratic (.A(A[6:2]), .sel(1'b1), .D(_0_quadratic_d));
  ROM #(.AddrBits(5), .Bits(32)) _1_sum_array_5 (.A(A[6:2]), .sel(1'b1), .D(_1_sum_array_5_d));
  ROM #(.AddrBits(5), .Bits(32)) _2_find_max_5 (.A(A[6:2]), .sel(1'b1), .D(_2_find_max_5_d));
  ROM #(.AddrBits(5), .Bits(32)) _3_fib_iter_10 (.A(A[6:2]), .sel(1'b1), .D(_3_fib_iter_10_d));
  ROM #(.AddrBits(5), .Bits(32)) _4_fib_iter_19 (.A(A[6:2]), .sel(1'b1), .D(_4_fib_iter_19_d));
  ROM #(.AddrBits(5), .Bits(32)) _5_fib_rec_10 (.A(A[6:2]), .sel(1'b1), .D(_5_fib_rec_10_d));
  ROM #(.AddrBits(5), .Bits(32)) _6_fib_rec_19 (.A(A[6:2]), .sel(1'b1), .D(_6_fib_rec_19_d));
  Multiplexer #(.Selector_Bits(4), .Bits(32)) multiplexer_1 (
    .sel(PN), .in_0(_0_quadratic_d), .in_1(_1_sum_array_5_d), .in_2(_2_find_max_5_d),
    .in_3(_3_fib_iter_10_d), .in_4(_4_fib_iter_19_d), .in_5(_5_fib_rec_10_d), .in_6(_6_fib_rec_19_d),
    .in_7({32{1'b0}}), .in_8({32{1'b0}}), .in_9({32{1'b0}}), .in_10({32{1'b0}}), .in_11({32{1'b0}}),
    .in_12({32{1'b0}}), .in_13({32{1'b0}}), .in_14({32{1'b0}}), .in_15({32{1'b0}}), .out(D));

  // Notes on the sheet:
  //   contents of _0_quadratic (hex, n*v repeats v):
  //   e3a00002,e3a01001,e3a02002,e3a03003,eb000000,eafffffe,e1a0c001,e00c0c90,e00c0c90,
  //   e08c3003,e1a0c002,e00c0c90,e08c3003,e1a00003,e12fff1e
  //   contents of _1_sum_array_5 (hex, n*v repeats v):
  //   e3a0d080,e24dd014,e3a00001,e58d0000,e3a00002,e58d0004,e3a00003,e58d0008,e3a00004,
  //   e58d000c,e3a00005,e58d0010,e1a0000d,e3a01005,eb000000,eafffffe,e3a02000,e3a03000,
  //   e1520001,a000004,e590c000,e083300c,e2822001,e2800004,eafffff8,e1a00003,e12fff1e
  //   contents of _2_find_max_5 (hex, n*v repeats v):
  //   e3a0d080,e24dd014,e3a00001,e58d0000,e3a00002,e58d0004,e3a00032,e58d0008,e3a00003,
  //   e58d000c,e3a00004,e58d0010,e1a0000d,e3a01005,eb000000,eafffffe,e3a03000,e590c000,
  //   e1a0200c,e2833001,e2800004,e590c000,e1530001,a000004,e15c0002,ca000000,eafffff7,e1a0200c,
  //   eafffff5,e1a00002,e12fff1e
  //   contents of _3_fib_iter_10 (hex, n*v repeats v):
  //   e3a0000a,e3a01000,e3a02000,e3a03001,e3a0c001,eb000000,eafffffe,e3500000,a000006,e1530000,
  //   a000005,e1a01002,e1a0200c,e081c002,e2833001,eafffff8,e12fff1e,e1a0000c,e12fff1e
  //   contents of _4_fib_iter_19 (hex, n*v repeats v):
  //   e3a00013,e3a01000,e3a02000,e3a03001,e3a0c001,eb000000,eafffffe,e3500000,a000006,e1530000,
  //   a000005,e1a01002,e1a0200c,e081c002,e2833001,eafffff8,e12fff1e,e1a0000c,e12fff1e
  //   contents of _5_fib_rec_10 (hex, n*v repeats v):
  //   e3a0000a,eb000000,eafffffe,e24dd010,e3500000,a00000f,e3500001,1a000001,e3a00001,ea00000b,
  //   e58de000,e58d0004,e2400001,ebfffff4,e1a01000,e58d1008,e59d0004,e2400002,ebffffef,
  //   e59d1008,e59de000,e0810000,e28dd010,e12fff1e
  //   contents of _6_fib_rec_19 (hex, n*v repeats v):
  //   e3a00013,eb000000,eafffffe,e24dd010,e3500000,a00000f,e3500001,1a000001,e3a00001,ea00000b,
  //   e58de000,e58d0004,e2400001,ebfffff4,e1a01000,e58d1008,e59d0004,e2400002,ebffffef,
  //   e59d1008,e59de000,e0810000,e28dd010,e12fff1e
  //   0- quadratic: x = 2, a = 1, b = 2, c = 3 => result = 11
  //   1- sum-array-5: [1, 2, 3, 4, 5] => result = 15
  //   2- find-max-5: [1, 2, 5, 3, 4] => result = 5
  //   3- fib-iter-10: result = 55
  //   4- fib-iter-19: result = 4181
  //   5- fib-rec-10: result = 55
  //   6- fib-rec-19: result = 4181
endmodule
