// Digital circuit processor_fixed_positions.dig as structural Verilog
module processor_fixed_positions (
  input  clk,
  input  [3:0] PN,
  output [31:0] FinalOutput
);

  wire a_mul, ALU1src, BL, BR, BX, C, clk_t, comparator_1_eq, dipswitch_1_out, i_dp, MR, mul, MW, N, RFW, V,
       Z;
  wire [1:0] ALU_op, EXT;
  wire [3:0] cond, multiplexer_3_out, multiplexer_5_out, multiplexer_6_out, multiplexer_7_out,
       multiplexer_8_out, NZCV;
  wire [23:0] b_offset;
  wire [27:24] iw;
  wire [31:0] add_1_s, add_2_s, alu_1_p4, data, multiplexer_1_out, multiplexer_4_out, multiplexer_9_out,
       multiplexer_10_out, pc_in, pc_out, r1, r2, r3, r4, r5, r6, r7, r8, r9, r10, r11, r12, r13, r14, r15,
       ramdualport_1_d, registerfile_1_rd0, sign_extend_all_1_extimm;

  // Probe on {cond, iw[27:26], i_dp, iw[24], b_offset[23:22], a_mul, b_offset[20:0]}
  and and_1 (clk_t, clk, dipswitch_1_out);
  DipSwitch dipswitch_1 (.out(dipswitch_1_out));
  Multiplexer #(.Bits(32)) multiplexer_1 (.sel(BR), .in_0(add_1_s), .in_1(multiplexer_10_out), .out(multiplexer_1_out));
  conditional_control_unit conditional_control_unit_1 (
    .iw({cond, iw[27:26], i_dp, iw[24], b_offset[23:22], a_mul, b_offset[20:0]}), .NZCV(NZCV), .CLK(clk_t),
    .RFW(RFW), .EXT(EXT), .ALUop(ALU_op), .ALU1src(ALU1src), .BR(BR), .BL(BL), .BX(BX), .mul(mul), .MR(MR),
    .MW(MW));
  Register #(.Bits(32), .isProgramCounter("true")) PC (.D(pc_in), .C(clk_t), .en(1'b1), .Q(pc_out));
  Multiplexer #(.Bits(32)) multiplexer_2 (.sel(BX), .in_0(multiplexer_1_out), .in_1(data), .out(pc_in));
  // Probe on FinalOutput
  // Probe on r1
  // Probe on r2
  // Probe on r3
  instruction_memory instruction_memory_1 (
    .A(pc_out), .PN(PN), .D({cond, iw[27:26], i_dp, iw[24], b_offset[23:22], a_mul, b_offset[20:0]}));
  Add #(.Bits(32)) add_1 (.a(pc_out), .b(32'h4), .c_i(1'b0), .s(add_1_s));  // open: c_o
  // Probe on r4
  // Probe on r5
  // Probe on r6
  // Probe on r7
  // Probe on cond
  // Probe on cond
  // Probe on cond
  Add #(.Bits(32)) add_2 (.a(add_1_s), .b(32'h4), .c_i(1'b0), .s(add_2_s));  // open: c_o
  // Probe on cond
  // Probe on r8
  // Probe on r9
  // Probe on r10
  // Probe on r11
  // Probe on iw[27:26]
  // Probe on {iw[27:26], i_dp, iw[24], b_offset[23]}
  // Probe on iw[27:26]
  // Probe on i_dp
  Multiplexer #(.Bits(4)) multiplexer_3 (.sel(BL), .in_0(b_offset[15:12]), .in_1(4'b1110), .out(multiplexer_3_out));
  Multiplexer #(.Bits(32)) multiplexer_4 (.sel(BL), .in_0(multiplexer_10_out), .in_1(add_1_s), .out(multiplexer_4_out));
  // Probe on r12
  // Probe on r13
  // Probe on r14
  // Probe on r15
  // Probe on pc_out
  // Probe on i_dp
  // Probe on a_mul
  // Probe on i_dp
  // Probe on iw[24]
  Multiplexer #(.Bits(4)) multiplexer_5 (.sel(BR), .in_0(b_offset[19:16]), .in_1(4'b1111), .out(multiplexer_5_out));
  Multiplexer #(.Bits(4)) multiplexer_6 (
    .sel(mul), .in_0(multiplexer_5_out), .in_1(b_offset[11:8]), .out(multiplexer_6_out));
  Multiplexer #(.Bits(4)) multiplexer_7 (
    .sel(MW), .in_0(b_offset[3:0]), .in_1(b_offset[15:12]), .out(multiplexer_7_out));
  Multiplexer #(.Bits(4)) multiplexer_8 (
    .sel(mul), .in_0(multiplexer_3_out), .in_1(b_offset[19:16]), .out(multiplexer_8_out));
  // Probe on {iw[24], b_offset[23:22], a_mul}
  // Probe on b_offset[20]
  // Probe on iw[24]
  // Probe on {b_offset[23:22], a_mul, b_offset[20:0]}
  // Probe on N
  // Probe on Z
  // Probe on C
  // Probe on V
  // Probe on b_offset[20]
  // Probe on b_offset[19:16]
  // Probe on b_offset[23]
  // Probe on b_offset[19:16]
  RegisterFile registerfile_1 (
    .ReadReg0(multiplexer_6_out), .ReadReg1(multiplexer_7_out), .WriteReg(multiplexer_8_out),
    .WriteData(multiplexer_4_out), .WriteEN(RFW), .CLK(clk_t), .PC(add_2_s), .RD0(registerfile_1_rd0),
    .RD1(data), .r0(FinalOutput), .r1(r1), .r2(r2), .r3(r3), .r4(r4), .r5(r5), .r6(r6), .r7(r7), .r8(r8),
    .r9(r9), .r10(r10), .r11(r11), .r12(r12), .r13(r13), .r14(r14), .r15(r15));
  // Probe on b_offset[19:16]
  // Probe on b_offset[15:12]
  // Probe on b_offset[22]
  // Probe on b_offset[15:12]
  // Probe on pc_in
  Comparator #(.Bits(32)) comparator_1 (.a(pc_in), .b(pc_out), .eq(comparator_1_eq));  // open: gt, lt
  // Probe on pc_out
  // Probe on b_offset[15:12]
  // Probe on b_offset[7:4]
  // Probe on a_mul
  // Probe on b_offset[3:0]
  // Probe on b_offset[11:0]
  LED Finished__RED (.in(comparator_1_eq));
  // Probe on b_offset[3:0]
  // Probe on b_offset[7:0]
  // Probe on b_offset[3:0]
  // Probe on b_offset[20]
  sign_extend_all sign_extend_all_1 (
    .iw({cond, iw[27:26], i_dp, iw[24], b_offset[23:22], a_mul, b_offset[20:0]}), .EXT(EXT),
    .extimm(sign_extend_all_1_extimm));
  Multiplexer #(.Bits(32)) multiplexer_9 (
    .sel(ALU1src), .in_0(data), .in_1(sign_extend_all_1_extimm), .out(multiplexer_9_out));
  // Probe on sign_extend_all_1_extimm
  // ALU alu_1: pin names not known; wires that end beside it: registerfile_1_rd0, multiplexer_9_out, ALU_op, alu_1_p4, NZCV, N, Z, C, V
  // Probe on ALU_op
  Multiplexer #(.Bits(32)) multiplexer_10 (.sel(MR), .in_0(alu_1_p4), .in_1(ramdualport_1_d), .out(multiplexer_10_out));
  RAMDualPort #(.AddrBits(9), .Bits(32)) ramdualport_1 (
    .A(alu_1_p4[10:2]), .Din(data), .str(MW), .C(clk_t), .ld(MR), .D(ramdualport_1_d));

  // Other names for the same wires on the sheet: imm[7:0] = b_offset[7:0]; immoff[11:0] = b_offset[11:0];
  //   iw (some bits) = {cond, i_dp, b_offset[23:22], a_mul, b_offset[20:0]}; rm[3:0] = b_offset[3:0];
  //   rm_mul[3:0] = b_offset[3:0]; opmul4[3:0] = b_offset[7:4]; rs_mul[3:0] = b_offset[11:8];
  //   rd[3:0] = b_offset[15:12]; rn_mul[3:0] = b_offset[15:12]; rd_mul[3:0] = b_offset[19:16];
  //   rn[3:0] = b_offset[19:16]; l_sdt = b_offset[20]; s_dp = b_offset[20]; s_mul = b_offset[20];
  //   b_offset[21] = a_mul; opc[3:0] = {iw[24], b_offset[23:22], a_mul}; w_sdt = a_mul; b_sdt = b_offset[22];
  //   opmul6[4:0] = {iw[27:26], i_dp, iw[24], b_offset[23]}; u_sdt = b_offset[23]; l_b = iw[24]; p_sdt = iw[24];
  //   i_sdt = i_dp; opb3 = i_dp; op2[1:0] = iw[27:26]; opmul2[1:0] = iw[27:26]; r0[31:0] = FinalOutput

  // Notes on the sheet:
  //   clk: Hz: 5000
  //   0- quadratic: x = 2, a = 1, b = 2, c = 3 => result = 11
  //   1- sum-array-5: [1, 2, 3, 4, 5] => result = 15
  //   2- find-max-5: [1, 2, 50, 3, 4] => result = 50
  //   3- fib-iter-10: result = 55
  //   4- fib-iter-19: result = 4181
  //   5- fib-rec-10: result = 55
  //   6- fib-rec-19: result = 4181
  //   DP
  //   MUL
  //   SDT
  //   B
  //   SP
  //   LR
  //   PC+8
  //   PC
endmodule
