// Digital circuit sign_extend_all.dig as structural Verilog
module sign_extend_all (
  input  [31:0] iw,
  input  [1:0] EXT,
  output [31:0] extimm
);

  wire [31:0] extend_output;
  wire [63:0] mul_1_mul;

  extend extend (.Input(iw), .Output(extend_output));
  Mul #(.Bits(32)) mul_1 (.a(32'h4), .b(extend_output), .mul(mul_1_mul));
  Multiplexer #(.Selector_Bits(2), .Bits(32)) multiplexer_1 (
    .sel(EXT), .in_0({{24{1'b0}}, iw[7:0]}), .in_1({{20{1'b0}}, iw[11:0]}), .in_2(mul_1_mul[31:0]),
    .in_3({32{1'b0}}), .out(extimm));
endmodule
